# Fritzing sketch CarSchematic (saved by Fritzing 0.9.3b)
breadboards: 1

parts:
  S3 = Pushbutton [part_number=bbb package=THT]
  Raspberry_Pi_1 = Raspberry Pi 3 [part_number=RPI-3-V1.2]
  read_USB = LED - 5mm [color="Red (660nm)" package="5 mm [THT]"]
  save_USB = LED - 5mm [color="Red (660nm)" package="5 mm [THT]"]
  collect_data = LED - 5mm [color="Red (660nm)" package="5 mm [THT]"]
  internal = Resistor [tolerance=±5% resistance=1k package=THT]
  internal4 = Resistor [tolerance=±5% resistance=1k package=THT]
  S7 = Pushbutton [package=THT]
  internal1 = Resistor [tolerance=±5% resistance=1k package=THT]
  S8 = Pushbutton [package=THT]
  nternal3 = Resistor [tolerance=±5% resistance=1k package=THT]
  internal5 = Resistor [tolerance=±5% resistance=1k package=THT]
  FubarinoSD1 = Fubarino SD [chip_label=FubarinoSD package="DIP (Dual Inline) [THT]"]  # not connected
  R2 = Resistor [tolerance=±5% resistance=470 package=THT]
  R3 = Resistor [tolerance=±5% resistance=470 package=THT]
  R4 = Resistor [tolerance=±5% resistance=470 package=THT]
  R5 = Resistor [tolerance=±5% resistance=470 package=THT]
  shutdown = LED - 5mm [color="Red (633nm)" package="5 mm [THT]"]
  autonomous = LED - 5mm [color="Red (660nm)" package="5 mm [THT]"]
  S10 = Pushbutton [package=THT]
  S11 = Pushbutton [package=THT]
  R6 = Resistor [tolerance=±5% resistance=470 package=THT]
  boot_pi = LED - 5mm [color="Red (633nm)" package="5 mm [THT]"]
  R7 = Resistor [tolerance=±5% resistance=470 package=THT]
  Boot_pi = Pushbutton [package=THT]
  internal6 = Resistor [tolerance=±5% resistance=100 package=THT]
  CONN1 = USB connector [package=THT]
  CONN2 = USB connector [package=THT]
  D1 = Rectifier Diode [part_number=1N4001 package="300 mil [THT]"]
  R8 = Resistor [tolerance=±5% resistance=470 package=THT]
  power_on = LED - 5mm [color="Red (633nm)" package="5 mm [THT]"]
  DIP-Relay1 = DIP-Relay-D31A [part_number=D31A*]

nets:
  GND: S3.leg0, S7.leg0, S8.leg0, R2.Pin_1, R3.Pin_1, R4.Pin_1, R5.Pin_1, S10.leg0, S11.leg0, R6.Pin_1, R7.Pin_1
  N1: S3.leg1, Raspberry_Pi_1.GPIO17, internal.Pin_0, autonomous.anode
  N2: Raspberry_Pi_1.GPIO2, read_USB.anode
  N3: Raspberry_Pi_1.GPIO3, save_USB.anode
  N4: Raspberry_Pi_1.GPIO4, collect_data.anode
  N5: Raspberry_Pi_1.GPIO27, shutdown.anode
  N6: Raspberry_Pi_1.GPIO22, boot_pi.anode
  N7: Raspberry_Pi_1.GPIO10, internal.Pin_1
  N8: Raspberry_Pi_1.GPIO9, internal1.Pin_1
  N9: Raspberry_Pi_1.GPIO11, nternal3.Pin_1
  N10: Raspberry_Pi_1.GPIO5, internal4.Pin_1
  N11: Raspberry_Pi_1.GPIO6, internal5.Pin_1
  N12: Raspberry_Pi_1.GPIO13, D1.anode
  N13: read_USB.cathode, R7.Pin_0
  N14: save_USB.cathode, R2.Pin_0
  N15: collect_data.cathode, R3.Pin_0
  N16: internal4.Pin_0, S10.leg1
  N17: S7.leg1, internal1.Pin_0
  N18: S8.leg1, nternal3.Pin_0
  N19: internal5.Pin_0, S11.leg1
  N20: R4.Pin_0, shutdown.cathode
  N21: R5.Pin_0, autonomous.cathode
  N22: R6.Pin_0, boot_pi.cathode
  N23: Boot_pi.leg0, CONN1.5V, DIP-Relay1.B2_Switch_Terminal_B
  N24: Boot_pi.leg1, internal6.Pin_0
  N25: internal6.Pin_1, D1.cathode, DIP-Relay1.COIL1_+
  N26: CONN1.chassis6, CONN2.5V, R8.Pin_1, DIP-Relay1.Coil2_-
  N27: CONN2.chassis6, power_on.anode, DIP-Relay1.A2_Switch_Terminal_A
  N28: R8.Pin_0, power_on.cathode

custom parts:
  Fubarino SD: Fubarino SD, v1.5, a chipKIT board.
